// Digital circuit Idea1_circuit.dig as structural Verilog
module Idea1_circuit (
  input  A,
  input  B,
  input  C,
  input  in_7,
  output Q_2,
  output Q_1,
  output Q_0
);

  wire and_1_out, and_2_out, and_3_out, and_8_out, and_9_out, and_10_out, and_11_out, and_12_out, and_13_out,
       and_14_out, and_15_out, and_16_out, and_17_out, and_18_out, and_19_out, and_20_out, MG, MR, MY,
       not_1_out, not_2_out, not_3_out, not_4_out, not_5_out, or_3_out, or_4_out, or_5_out, Q_0NOT, Q_1NOT,
       Q_2NOT, SG, SR, SY;

  and and_1 (and_1_out, Q_1NOT, Q_0);
  and and_2 (and_2_out, Q_2NOT, Q_0);
  and and_3 (and_3_out, Q_2NOT, Q_1);
  or or_1 (MR, Q_2, and_1_out);
  and and_4 (MY, Q_1, Q_0);
  and and_5 (MG, Q_1, Q_0NOT);
  or or_2 (SR, and_2_out, and_3_out);
  and and_6 (SY, Q_2, Q_1NOT);
  and and_7 (SG, Q_2, Q_0NOT);
  not not_1 (not_1_out, A);
  not not_2 (not_2_out, B);
  not not_3 (not_3_out, Q_2);
  not not_4 (not_4_out, Q_1);
  not not_5 (not_5_out, Q_0);
  and and_8 (and_8_out, not_1_out, not_2_out, Q_0, not_4_out, not_3_out);
  and and_9 (and_9_out, A, B, Q_0, not_3_out);
  and and_10 (and_10_out, not_1_out, not_2_out, not_5_out, Q_2);
  and and_11 (and_11_out, A, B, not_5_out, Q_2);
  and and_12 (and_12_out, not_1_out, not_2_out, not_5_out, Q_1);
  and and_13 (and_13_out, A, B, not_5_out, not_3_out);
  and and_14 (and_14_out, not_1_out, not_2_out, Q_0, Q_2);
  and and_15 (and_15_out, A, B, Q_0, Q_2);
  and and_16 (and_16_out, A, not_5_out, not_4_out, not_3_out);
  and and_17 (and_17_out, not_1_out, not_2_out, not_5_out);
  and and_18 (and_18_out, not_1_out, not_2_out, Q_1);
  and and_19 (and_19_out, A, B);
  and and_20 (and_20_out, not_5_out, not_4_out, not_3_out);
  or or_3 (or_3_out, and_8_out, and_9_out, and_10_out, and_11_out);
  or or_4 (or_4_out, and_12_out, and_13_out, and_14_out, and_15_out, and_16_out);
  or or_5 (or_5_out, and_17_out, and_18_out, and_19_out, and_20_out);
  D_FF_AS d_ff_as_1 (.Set(1'b0), .D(or_3_out), .C(C), .Clr(in_7), .Q(Q_2), .nQ(Q_2NOT));
  D_FF_AS d_ff_as_2 (.Set(1'b0), .D(or_4_out), .C(C), .Clr(in_7), .Q(Q_1), .nQ(Q_1NOT));
  D_FF_AS d_ff_as_3 (.Set(1'b0), .D(or_5_out), .C(C), .Clr(in_7), .Q(Q_0), .nQ(Q_0NOT));
  // Probe state on {Q_2, Q_1, Q_0}
  LED led_1 (.in(MR));
  LED led_2 (.in(MY));
  LED led_3 (.in(MG));
  LED led_4 (.in(SR));
  LED led_5 (.in(SY));
  LED led_6 (.in(SG));

  // Notes on the sheet:
  //   C: Hz: 2
  //   Main Street
  //   Side Avenue
endmodule
